# Fritzing sketch PumpFlow v0.5.0 (saved by Fritzing 0.9.2b)
circuit board: 5.13295cm x 8.15553cm
breadboards: 1

parts:
  Micro = Adafruit Metro Mini
  Top_LED = screw terminal, 2 pins
  RS232 = screw terminal, 3 pins
  24V_Supply = screw terminal, 2 pins
  RPM = screw terminal, 3 pins
  Pressure = screw terminal, 3 pins
  Bott_LED = screw terminal, 2 pins
  MAX232 = Sparkfun MAX3232
  R1 = Resistor [tolerance=±5% resistance=1k package=THT]
  TSR1 = Header 3 [package=molex-1x3_lock]
  ADS1115 = ADS1115 16-bit ADC Breakout
  R2 = Resistor [tolerance=±1% resistance=240 package=THT]

nets:
  N1: Micro.3V, Micro.D3
  5V: Micro.5V, Micro.D2, RPM.pin1, RPM.pin3, R1.Pin_0, R1.Pin_1, ADS1115.VDD
  GND: Micro.GND#20, Top_LED.pin2, RS232.pin3, 24V_Supply.pin1, RPM.pin2, Pressure.pin1, Bott_LED.pin2, MAX232.GND, TSR1.2, ADS1115.GND, ADS1115.ADDR, R2.Pin_0
  N2: Micro.A4, ADS1115.SDA
  N3: Micro.A5, ADS1115.SCL
  N4: Micro.D5, Top_LED.pin1
  N5: Micro.D6, Bott_LED.pin1
  N6: Micro.D10, MAX232.T1IN
  N7: Micro.D11, MAX232.R1OUT
  N8: RS232.pin1, MAX232.T1OUT
  N9: RS232.pin2, MAX232.R1IN
  N10: 24V_Supply.pin2, Pressure.pin3, TSR1.1
  N11: Pressure.pin2, ADS1115.A0, R2.Pin_1
  N12: MAX232.3V-5.5V, TSR1.3

custom parts:
  Adafruit Metro Mini: Adafruit arduino
  Sparkfun MAX3232: MAX3232 Breakout Board
  ADS1115 16-bit ADC Breakout: ADS1015 12-bit I2C ADC+PGA Breakout
